# Fritzing sketch encoderElectronic (saved by Fritzing 0.9.3b)
breadboards: 1

parts:
  Q1 = LTR-301 [package=ltr-301]
  Composant1 = Arduino Mega 2560 (Rev3)
  R3 = Resistor [package="0402 [SMD]"]
  R1 = Resistor 10K [package="0402 [SMD]"]
  D1 = LTE-302 [package=lte-302]
  R6 = Resistor150 [package="0402 [SMD]"]
  BC547 = NPN-Transistor [package="TO92 [THT]"]
  2N222A = TRANSISTOR_NPN - 2N2222 [package=to-92]
  U1 = Voltage Regulator - 5V [package="DPak [SMD]"]

nets:
  N1: Q1.C, R1.Pin_0
  N2: Q1.E, R3.Pin_1, D1.C, BC547.B
  GND: Composant1.A8, Composant1.GND, R1.Pin_1, R6.Pin_1, BC547.E, 2N222A.E, U1.GND
  N3: Composant1.D48, 2N222A.B
  N4: R3.Pin_0, BC547.C
  N5: 2N222A.C, U1.output_voltage

notes:
  IR emitter
  IR receiver
  wheel encoder
  power

custom parts:
  Resistor: Resistor Basic schematic elements and footprints for 0603, 1206, and PTH resistors.
  Resistor 10K: Resistor Basic schematic elements and footprints for 0603, 1206, and PTH resistors.
  Resistor150: Resistor Basic schematic elements and footprints for 0603, 1206, and PTH resistors.
  TRANSISTOR_NPN - 2N2222: Generic NPN BJT. MMBT2222 is the common NPN we use. Double check against datasheet- not all devices are the same!
