# Fritzing sketch encoderElectronicV2 (saved by Fritzing 0.9.4)
breadboards: 1

parts:
  D2 = LTE-302 [package=lte-302]
  D3 = IR Receiver [package=lte-302]
  R1 = Resistor [tolerance=±5% resistance=1k package=THT]
  R2 = Resistor [tolerance=±5% resistance=150 package=THT]
  R3 = Resistor [tolerance=±5% resistance=10k package=THT]
  R4 = Resistor [tolerance=±5% resistance=1k package=THT]
  Q1 = NPN-Transistor [package="TO92 [THT]"]
  2N222A1 = TRANSISTOR_NPN - 2N2222 [package=to-92]
  Composant1 = Arduino Uno (Rev3) - ICSP

nets:
  N1: D2.A, D3.Cathode, R3.Pin_0, 2N222A1.E
  N2: D2.C, R2.Pin_0
  N3: D3.Anode, R1.Pin_1, R4.Pin_1
  N4: R1.Pin_0, R2.Pin_1, Q1.E, Composant1.GND
  N5: R3.Pin_1, Q1.C, Composant1.A0
  N6: R4.Pin_0, Q1.B
  N7: 2N222A1.B, Composant1.D8

notes:
  IR emitter
  IR receiver
  5v power

custom parts:
  IR Receiver: 940nm IR receiver
  TRANSISTOR_NPN - 2N2222: Generic NPN BJT. MMBT2222 is the common NPN we use. Double check against datasheet- not all devices are the same!
