# Fritzing sketch encodersPowerSwitch (saved by Fritzing 0.9.3b)
breadboards: 1

parts:
  Q1 = NPN-Transistor [package="TO92 [THT]"]
  Q2 = NPN-Transistor [package="TO92 [THT]"]
  R1 = Resistor [package="0402 [SMD]"]

nets:
  N1: Q1.B, Q2.B, R1.Pin_0
  N2: Q1.C, Q2.C

notes:
  encoder 1 power
  encoder 2 power
  +5V power
  Arduino Power PIN
  2N222A

custom parts:
  Resistor: Resistor Basic schematic elements and footprints for 0603, 1206, and PTH resistors.
