# Fritzing sketch voltageDividors (saved by Fritzing 0.9.3b)
breadboards: 2

parts:
  R2 = 1Mg Ω Resistor [package=THT]
  R4 = 1Mg Ω Resistor [package=THT]
  R6 = 1Mg Ω Resistor [package=THT]
  R7 = 1Mg Ω Resistor [package=THT]
  R9 = 680k Ω Resistor [package=THT]
  R12 = 680k Ω Resistor [package=THT]
  R13 = 1Mg Ω Resistor [package=THT]
  R14 = 680k Ω Resistor [package=THT]
  R15 = 1Mg Ω Resistor [package=THT]
  R18 = 1Mg Ω Resistor [package=THT]
  R19 = 1Mg Ω Resistor [package=THT]
  Composant1 = Arduino Mega ADK (Rev3)
  R20 = 1Mg Ω Resistor [package=THT]
  R21 = 1Mg Ω Resistor [package=THT]
  VCC1 = Battery
  U1 = LIPO-2000mAh [package=lipo-2000]

nets:
  N1: R2.Pin_0, VCC1.+
  N2: R2.Pin_1, R13.Pin_0
  N3: R4.Pin_1, R14.Pin_0
  N4: R6.Pin_0, R9.Pin_1
  N5: R6.Pin_1, R7.Pin_0, Composant1.A1
  N6: R9.Pin_0, R12.Pin_1, R15.Pin_1, R19.Pin_0, Composant1.GND, R20.Pin_1, R21.Pin_0
  N7: R12.Pin_0, R13.Pin_1, Composant1.A2
  N8: R14.Pin_1, R15.Pin_0, Composant1.A3
  N9: R18.Pin_0, R19.Pin_1, Composant1.A0
  N10: R20.Pin_0, VCC1.-
  N11: R21.Pin_1, U1.-

notes:
  10 x 1.2 V for motors
  12V for electronics
  10v regulators
  9 & 5V regulators
  5v regulators

custom parts:
  1Mg Ω Resistor: A generic resistor (0.25W)
  680k Ω Resistor: A generic resistor (0.25W)
  680k Ω Resistor: A generic resistor (0.25W)
